# Fritzing sketch diagram (saved by Fritzing 0.9.2b)
breadboards: 1

parts:
  Arduino_nano = Arduino Nano (Rev3.0)
  Led_strip = ws2812b [package="smd 2812b"]
  S1 = SWITCH-MOMENTARY-2 [package=tactile-pth-12mm]
  S2 = SWITCH-MOMENTARY-2 [package=tactile-pth-12mm]
  S3 = SWITCH-MOMENTARY-2 [package=tactile-pth-12mm]
  S4 = SWITCH-MOMENTARY-2 [package=tactile-pth-12mm]
  U1 = MIDI_CONN_FEMALE_SUPPORT [package=din_5_female_support]
  R1 = Resistor [tolerance=±5% resistance=220 package="0805 [SMD]"]

nets:
  N1: Arduino_nano.D1/TX, R1.Pin_1
  GND: Arduino_nano.GND, Led_strip.VSS, S1.2, S2.2, S3.2, S4.2, U1.NC2
  N2: Arduino_nano.D2, S1.1
  N3: Arduino_nano.D3, S2.1
  N4: Arduino_nano.D4, S3.1
  N5: Arduino_nano.D5, S4.1
  N6: Arduino_nano.D12/MISO, Led_strip.DIN
  5V: Arduino_nano.5V, Led_strip.VDD, U1.MIDI_IN
  N7: U1.MIDI_OUT, R1.Pin_0
